# Fritzing sketch Untitled Sketch (saved by Fritzing 0.9.5d)
breadboards: 1

parts:
  KY-1 = keyes
  S1 = Pushbutton [package="[SMD]"]
  S2 = Momentary Switch [package=ksa_sealed_tac_switch]
  MH-ET_LIVE_ESP32_DEVKIT1 = MH-ET LIVE ESP32 DEVKIT
  Power_plug1 = Power plug
  R1 = Resistor [tolerance=±5% resistance=220 package=THT]
  LED1 = LED - 5mm [color="Red (633nm)" package="5 mm [THT]"]

nets:
  N1: KY-1.connector0, LED1.cathode
  N2: KY-1.connector1, MH-ET_LIVE_ESP32_DEVKIT1.connector63, Power_plug1.VCC, R1.Pin_1
  N3: KY-1.connector2, MH-ET_LIVE_ESP32_DEVKIT1.connector64
  N4: S1.Pin_1, S1.Pin_2, MH-ET_LIVE_ESP32_DEVKIT1.connector58
  N5: S1.Pin_3, S1.Pin_4, MH-ET_LIVE_ESP32_DEVKIT1.connector59
  N6: S2.3, MH-ET_LIVE_ESP32_DEVKIT1.connector79
